// Logisim project Decodeur_d_instructions.circ as structural Verilog: 2 circuits, main circuit main
module main (
  input  in_1,
  input  in_2,
  input  [31:0] in_3
);

  wire banc_reg_1_p2, banc_reg_1_p7, decodeur_1_imm_reg;
  wire [1:0] decodeur_1_op;
  wire [3:0] decodeur_1_rd, decodeur_1_rot, decodeur_1_rs1, decodeur_1_rs2;
  wire [7:0] decodeur_1_imm;
  wire [31:0] banc_reg_1_p8, banc_reg_1_p10, shifter_1_out;

  Decodeur decodeur_1 (
    .in_1(in_3), .Rs1(decodeur_1_rs1), .Rs2(decodeur_1_rs2), .Rd(decodeur_1_rd), .Imm(decodeur_1_imm),
    .Rot(decodeur_1_rot), .Imm_Reg(decodeur_1_imm_reg), .Op(decodeur_1_op));
  Shifter #(.shift("rr"), .width(32)) shifter_1 (
    .in({{24{1'b0}}, decodeur_1_imm}), .\dist ({decodeur_1_rot, 1'b0}), .out(shifter_1_out));
  // banc_reg banc_reg_1: pin names not known; wires that end beside it: in_1, banc_reg_1_p2, decodeur_1_rs1, decodeur_1_rs2, decodeur_1_rd, in_2, banc_reg_1_p7, banc_reg_1_p8, banc_reg_1_p7, banc_reg_1_p10, decodeur_1_op
  Multiplexer #(.width(32)) multiplexer_1 (
    .in0(banc_reg_1_p8), .in1(shifter_1_out), .out(banc_reg_1_p10), .sel(decodeur_1_imm_reg));
  // ALU alu_1: pin names not known; wires that end beside it: banc_reg_1_p2
endmodule

module Decodeur (
  input  [31:0] in_1,
  output [3:0] Rs1,
  output [3:0] Rs2,
  output [3:0] Rd,
  output [7:0] Imm,
  output [3:0] Rot,
  output Imm_Reg,
  output [1:0] Op
);

  wire and_1_out, not_1_out;

  and and_1 (and_1_out, not_1_out, in_1[23]);
  or or_1 (Op[1], and_1_out, in_1[22]);
  not not_1 (not_1_out, in_1[24]);
  or or_2 (Op[0], in_1[22], in_1[21]);

  assign Imm = in_1[7:0];
  assign Imm_Reg = in_1[25];
  assign Rd = in_1[15:12];
  assign Rot = in_1[11:8];
  assign Rs1 = in_1[19:16];
  assign Rs2 = in_1[3:0];
endmodule
