// Logisim project unite_de_condition.circ as structural Verilog: 3 circuits, main circuit main
module main (
  input  in_1,
  input  in_2
);

  wire banc_reg_1_p2, banc_reg_1_p8, clock_1_out, clock_2_out, decodeur_1_imm_reg;
  wire [1:0] decodeur_1_op;
  wire [3:0] decodeur_1_rd, decodeur_1_rot, decodeur_1_rs1, decodeur_1_rs2;
  wire [7:0] decodeur_1_imm;
  wire [23:0] register_1_q_2;
  wire [31:0] adder_1_out, banc_reg_1_p9, banc_reg_1_p11, ram_1_dout, register_1_q, shifter_1_out;

  Adder #(.width(32)) adder_1 (
    .a({register_1_q[31:26], register_1_q_2, register_1_q[1:0]}), .b(32'h4), .out(adder_1_out));  // open: cin, cout
  // Probe on {register_1_q[31:26], register_1_q_2, register_1_q[1:0]}
  Register #(.width(32)) register_1 (
    .D(adder_1_out), .en(1'b1), .clk(clock_1_out),
    .Q({register_1_q[31:26], register_1_q_2, register_1_q[1:0]}), .clr(in_1));
  Clock clock_1 (.out(clock_1_out));
  Decodeur decodeur_1 (
    .in_1(ram_1_dout), .Rs1(decodeur_1_rs1), .Rs2(decodeur_1_rs2), .Rd(decodeur_1_rd), .Imm(decodeur_1_imm),
    .Rot(decodeur_1_rot), .Imm_Reg(decodeur_1_imm_reg), .Op(decodeur_1_op));  // open: cond
  Clock clock_2 (.out(clock_2_out));
  Shifter #(.shift("rr"), .width(32)) shifter_1 (
    .in({{24{1'b0}}, decodeur_1_imm}), .\dist ({decodeur_1_rot, 1'b0}), .out(shifter_1_out));
  // Probe on banc_reg_1_p8
  // banc_reg banc_reg_1: pin names not known; wires that end beside it: clock_2_out, banc_reg_1_p2, decodeur_1_rs1, decodeur_1_rs2, decodeur_1_rd, in_2, {register_1_q[31:26], register_1_q_2, register_1_q[1:0]}, banc_reg_1_p8, banc_reg_1_p9, banc_reg_1_p8, banc_reg_1_p11, decodeur_1_op
  Multiplexer #(.width(32)) multiplexer_1 (
    .in0(banc_reg_1_p9), .in1(shifter_1_out), .out(banc_reg_1_p11), .sel(decodeur_1_imm_reg));
  // Probe on ram_1_dout
  RAM #(.addrWidth(24), .asyncread("true"), .dataWidth(32)) ram_1 (
    .addr(register_1_q_2), .oe(1'b1), .dout(ram_1_dout));  // open: we, clk, din
  // ALU alu_1: pin names not known; wires that end beside it: banc_reg_1_p2
endmodule

module Decodeur (
  input  [31:0] in_1,
  output [3:0] Rs1,
  output [3:0] Rs2,
  output [3:0] Rd,
  output [7:0] Imm,
  output [3:0] Rot,
  output Imm_Reg,
  output [1:0] Op,
  output [3:0] cond
);

  wire and_1_out, not_1_out;

  and and_1 (and_1_out, not_1_out, in_1[23]);
  or or_1 (Op[1], and_1_out, in_1[22]);
  not not_1 (not_1_out, in_1[24]);
  or or_2 (Op[0], in_1[22], in_1[21]);

  assign cond = in_1[31:28];
  assign Imm = in_1[7:0];
  assign Imm_Reg = in_1[25];
  assign Rd = in_1[15:12];
  assign Rot = in_1[11:8];
  assign Rs1 = in_1[19:16];
  assign Rs2 = in_1[3:0];
endmodule

module gest_cond (
  input  [3:0] cond,
  input  [3:0] NZCV,
  input  MaJ,
  output exec
);

  wire and_1_out, and_2_out, and_3_out, clock_1_out, decoder_1_out0, decoder_1_out1, decoder_1_out2,
       not_1_out;
  wire [3:0] register_1_q;

  Clock clock_1 (.out(clock_1_out));
  Decoder #(.enable("false"), .select(4)) decoder_1 (
    .out0(decoder_1_out0), .out1(decoder_1_out1), .out2(decoder_1_out2), .sel(cond));  // open: out3, out4, out5, out6, out7, out8, out9, out10, out11, out12, out13, out14, out15
  Register #(.width(4)) register_1 (.D(NZCV), .en(MaJ), .clk(clock_1_out), .Q(register_1_q));  // open: clr
  and and_1 (and_1_out, decoder_1_out0, register_1_q[2]);
  not not_1 (not_1_out, register_1_q[2]);
  and and_2 (and_2_out, decoder_1_out1, not_1_out);
  and and_3 (and_3_out, decoder_1_out2, register_1_q[1]);
  or or_1 (exec, and_1_out, and_2_out, and_3_out);
endmodule
